// Logisim project Dcache_control.circ as structural Verilog: 1 circuit, main circuit main
module main (
  input  a,
  input  b,
  input  unk1,
  input  unk2
);

  wire c_out, controlled_buffer_1_out, controlled_buffer_3_out, controlled_buffer_4_out, not_1_out,
       not_2_out, not_3_out, not_4_out, not_5_out, not_6_out, not_7_out, not_8_out, not_9_out, not_10_out,
       not_11_out;

  Clock #(.highDuration(4), .lowDuration(4)) c (.out(c_out));
  not not_1 (not_1_out, a);
  not not_2 (not_2_out, b);
  not not_3 (not_3_out, c_out);
  not not_4 (not_4_out, not_1_out);
  not not_5 (not_5_out, not_3_out);
  not not_6 (not_6_out, not_5_out);
  not not_7 (not_7_out, not_4_out);
  assign controlled_buffer_1_out = not_7_out ? 1'b1 : 1'bz;  // Controlled_Buffer controlled_buffer_1
  not not_8 (not_8_out, not_9_out);
  not not_9 (not_9_out, not_6_out);
  not not_10 (not_10_out, not_8_out);
  not not_11 (not_11_out, unk2);
  assign controlled_buffer_1_out = not_11_out ? 1'b1 : 1'bz;  // Controlled_Buffer controlled_buffer_2
  assign controlled_buffer_3_out = not_3_out ? controlled_buffer_4_out : 1'bz;  // Controlled_Buffer controlled_buffer_3
  assign controlled_buffer_4_out = not_10_out ? 1'b0 : 1'bz;  // Controlled_Buffer controlled_buffer_4
  assign controlled_buffer_1_out = not_2_out ? controlled_buffer_3_out : 1'bz;  // Controlled_Buffer controlled_buffer_5
  assign controlled_buffer_1_out = unk1 ? controlled_buffer_3_out : 1'bz;  // Controlled_Buffer controlled_buffer_6

  // Notes on the sheet:
  //   falling edge (negedge) detect
  //   if (a == 0 || unk2 == 0) out = 1;
  //   else out = Z;
  //   else if ((b == 0 || unk1) && negedge c) out = 0; 
endmodule
